# Fritzing sketch alexa-pi (saved by Fritzing 0.8.7b)
breadboards: 1

parts:
  Raspberry_Pi_B_rev1 = Raspberry Pi B rev1
  S1 = Pushbutton [package="[THT]"]
  LED1 = RGB LED (com. cathode, rgb) [package="5 mm [THT]"]

nets:
  N1: Raspberry_Pi_B_rev1.GND, S1.Pin_1, S1.Pin_2, LED1.common_cathode
  N2: Raspberry_Pi_B_rev1.GPIO_18, S1.Pin_3, S1.Pin_4
  N3: Raspberry_Pi_B_rev1.GPIO_24, LED1.red_anode
  N4: Raspberry_Pi_B_rev1.GPIO_25, LED1.green_anode
